// Digital circuit TST01.dig as structural Verilog
module TST01 (
  input  [7:0] Data
);

  wire Connect_out, mqttoutbyte_1_p4, Send_out;

  DipSwitch Connect (.out(Connect_out));
  Button Send (.out(Send_out));
  // MqttOutByte #(.mqttTopic("/digital/mqtt/test01")) mqttoutbyte_1: pin names not known; wires that end beside it: Data, Connect_out, Send_out, mqttoutbyte_1_p4
  LED Connected (.in(mqttoutbyte_1_p4));
endmodule
