// Digital circuit TST02.dig as structural Verilog
module TST02 (
  output [7:0] Data
);

  wire Connect_out, mqttinbyte_1_p3, Receive_out;

  DipSwitch Connect (.out(Connect_out));
  Button Receive (.out(Receive_out));
  // MqttInByte #(.mqttTopic("/digital/mqtt/test01")) mqttinbyte_1: pin names not known; wires that end beside it: Connect_out, Receive_out, mqttinbyte_1_p3, Data
  LED led_1 (.in(mqttinbyte_1_p3));
endmodule
