// Digital circuit TST02a.dig as structural Verilog
module TST02a (
  input  clk,
  input  in_3,
  output [7:0] Data
);

  wire and_1_out, Connect_out, mqttinbyte_1_p3;

  and and_1 (and_1_out, clk, in_3);
  DipSwitch Connect (.out(Connect_out));
  // MqttInByte #(.mqttTopic("/digital/mqtt/test01")) mqttinbyte_1: pin names not known; wires that end beside it: Connect_out, and_1_out, mqttinbyte_1_p3, Data
  LED led_1 (.in(mqttinbyte_1_p3));
endmodule
