// Digital circuit TST01.dig as structural Verilog
module TST01 (
  input  [7:0] in_1
);

  wire button_1_out, dipswitch_1_out, mqttoutbyte_1_p4;

  Button button_1 (.out(button_1_out));
  DipSwitch dipswitch_1 (.out(dipswitch_1_out));
  // MqttOutByte mqttoutbyte_1: pin names not known; wires that end beside it: in_1, dipswitch_1_out, button_1_out, mqttoutbyte_1_p4
  LED led_1 (.in(mqttoutbyte_1_p4));
endmodule
